// Logisim project Collision.circ as structural Verilog: 1 circuit, main circuit main
module main (
);

  wire and_1_out, and_2_out, and_3_out, and_4_out, and_5_out, and_6_out, and_7_out, and_8_out, button_1_out,
       controlled_buffer_1_out, not_1_out, or_1_out, or_2_out, or_3_out, or_4_out, ram_1_p5, undriven,
       undriven_2, undriven_3, undriven_4, undriven_5, undriven_6, undriven_7, undriven_8, undriven_9,
       undriven_10, undriven_11, undriven_12, undriven_13, undriven_14, undriven_15, undriven_16,
       undriven_17, undriven_18, undriven_19, undriven_20, undriven_21, undriven_22, undriven_23,
       undriven_24, undriven_25;
  wire [7:0] counter_1_q;

  and and_1 (and_1_out, undriven, undriven_2);
  and and_2 (and_2_out, undriven_3, undriven_4);
  and and_3 (and_3_out, undriven_5, undriven_6);
  and and_4 (and_4_out, undriven_7, undriven_8);
  and and_5 (and_5_out, undriven_9, undriven_10);
  and and_6 (and_6_out, undriven_11, undriven_12);
  and and_7 (and_7_out, undriven_13, undriven_14);
  and and_8 (and_8_out, undriven_15, undriven_16);
  or or_1 (or_1_out, and_1_out, and_2_out, and_4_out);
  or or_2 (or_2_out, and_5_out, and_6_out, and_7_out, and_8_out);
  or or_3 (or_3_out, or_1_out, or_2_out);
  not not_1 (not_1_out, or_3_out);
  Button button_1 (.out(button_1_out));
  assign controlled_buffer_1_out = or_4_out ? not_1_out : 1'bz;  // Controlled_Buffer controlled_buffer_1
  or or_4 (or_4_out, undriven_17, undriven_18, undriven_19, undriven_20, undriven_21, undriven_22, undriven_23, undriven_24);
  Counter counter_1 (.Q(counter_1_q), .clk(controlled_buffer_1_out));  // open: load, D, count, carry, clr
  // RAM #(.addrWidth(2), .dataWidth(3)) ram_1: pin names not known; wires that end beside it: counter_1_q, counter_1_q, counter_1_q, button_1_out, ram_1_p5
  _7_Segment_Display u_7_segment_display_1 (
    .g(undriven_25), .f(undriven_25), .a(undriven_25), .b(undriven_25), .e(ram_1_p5), .d(ram_1_p5),
    .c(ram_1_p5), .dp(ram_1_p5));

  // Notes on the sheet:
  //   Bird bit
  //   Col.2 display
  //   Bird bit
  //   Col.2 display
  //   Bird bit
  //   Col.2 display
  //   Bird bit
  //   Col.2 display
  //   Bird bit
  //   Col.2 display
  //   Bird bit
  //   Col.2 display
  //   Bird bit
  //   Col.2 display
  //   Bird bit
  //   Col.2 display
  //   Row 1
  //   Row 2
  //   Row 3
  //   Row 4
  //   Row 5
  //   Row 6
  //   Row 7
  //   Row 8
  //   if collision, 1
  //   Shift Register Outputs
  //   Clock Logic 
endmodule
