// Logisim project Bird.circ as structural Verilog: 1 circuit, main circuit main
module main (
);

  wire button_1_out, clock_1_out, clock_2_out, decoder_1_out0, decoder_1_out1, decoder_1_out2,
       decoder_1_out3, decoder_1_out4, decoder_1_out5, decoder_1_out6, decoder_1_out7, j_k_ff_1_q;
  wire [2:0] _4029_q;

  Button button_1 (.out(button_1_out));
  Clock clock_1 (.out(clock_1_out));
  Clock clock_2 (.out(clock_2_out));
  Counter #(.width(3), .max('h7)) _4029 (
    .load(j_k_ff_1_q), .Q(_4029_q), .clk(clock_1_out));  // open: D, count, carry, clr
  J_K_Flip_Flop j_k_ff_1 (.J(1'b1), .clk(clock_2_out), .K(1'b1), .Q(j_k_ff_1_q));  // open: Qn, preset, en, reset
  Decoder #(.select(3)) decoder_1 (
    .out0(decoder_1_out0), .out1(decoder_1_out1), .out2(decoder_1_out2), .out3(decoder_1_out3),
    .out4(decoder_1_out4), .out5(decoder_1_out5), .out6(decoder_1_out6), .out7(decoder_1_out7),
    .sel(_4029_q), .en(_4029_q[0]));
  // Pins of 1 and 3 bits meet at _4029_q

  // Notes on the sheet:
  //   Astable
  //   Monostable
  //   Preset 100
  //   JK Flip Flop
  //   Bird bits on column 2
endmodule
