// Logisim project Clock.circ as structural Verilog: 1 circuit, main circuit main
module main (
);

  wire and_1_out, and_2_out, and_3_out, and_4_out, and_5_out, and_6_out, and_7_out, and_8_out, button_1_out,
       clock_1_out, demultiplexer_1_out0, demultiplexer_1_out1, demultiplexer_1_out2, demultiplexer_1_out4,
       demultiplexer_1_out5, demultiplexer_1_out6, demultiplexer_1_out7, j_k_ff_1_q, or_1_out, undriven,
       undriven_2, xor_1_out;
  wire [2:0] counter_1_q, undriven_3;

  Button button_1 (.out(button_1_out));
  Clock clock_1 (.out(clock_1_out));
  J_K_Flip_Flop j_k_ff_1 (.J(1'b1), .clk(button_1_out), .K(1'b1), .Q(j_k_ff_1_q));  // open: Qn, preset, en, reset
  Counter #(.width(3), .max('h7)) counter_1 (.Q(counter_1_q), .clk(clock_1_out));  // open: load, D, count, carry, clr
  xor xor_1 (xor_1_out, j_k_ff_1_q, undriven);
  Demultiplexer #(.select(3)) demultiplexer_1 (
    .out0(demultiplexer_1_out0), .out1(demultiplexer_1_out1), .out2(demultiplexer_1_out2),
    .out3(counter_1_q[0]), .out4(demultiplexer_1_out4), .out5(demultiplexer_1_out5),
    .out6(demultiplexer_1_out6), .out7(demultiplexer_1_out7), .in(xor_1_out), .sel(undriven_3),
    .en(undriven_2));
  and and_1 (and_1_out, demultiplexer_1_out4, counter_1_q[0]);
  and and_2 (and_2_out, demultiplexer_1_out0, counter_1_q[0]);
  and and_3 (and_3_out, demultiplexer_1_out5, counter_1_q[0]);
  and and_4 (and_4_out, demultiplexer_1_out1, counter_1_q[0]);
  and and_5 (and_5_out, demultiplexer_1_out6, counter_1_q[0]);
  and and_6 (and_6_out, demultiplexer_1_out2, counter_1_q[0]);
  and and_7 (and_7_out, counter_1_q[0], counter_1_q[0]);
  and and_8 (and_8_out, demultiplexer_1_out7, counter_1_q[0]);
  or or_1 (or_1_out, and_2_out, and_4_out, and_6_out, and_7_out, and_1_out, and_3_out, and_5_out, and_8_out);
  // Pins of 1 and 3 bits meet at counter_1_q

  // Notes on the sheet:
  //   if Collision = 1
  //   Score Counter
  //   Final Clock for Shifting
endmodule
