// Logisim project Display.circ as structural Verilog: 1 circuit, main circuit main
module main (
);

  wire or_1_out, or_2_out, or_3_out, or_4_out, or_5_out, or_6_out, or_7_out, or_8_out, undriven, undriven_2,
       undriven_3, undriven_4, undriven_5, undriven_6, undriven_7, undriven_8, undriven_9, undriven_10,
       undriven_11, undriven_12, undriven_13, undriven_14, undriven_15, undriven_16, undriven_17,
       undriven_18, undriven_19, undriven_20, undriven_21, undriven_22, undriven_23, undriven_24,
       undriven_25, undriven_26, undriven_27, undriven_28, undriven_29, undriven_30, undriven_31, undriven_32;

  Shift_Register shift_register_1 (
    .shift(undriven_2), .load(undriven_9), .d0(undriven_9), .d1(undriven_9), .d2(undriven_9),
    .d3(undriven_9), .d4(undriven_9), .d5(undriven_17), .d6(undriven_9));  // open: in, clk, out, clr, q0, q1, q2, q3, q4, q5, q6, d7, q7
  Shift_Register shift_register_2 (
    .in(undriven_3), .load(undriven_10), .d0(undriven_10), .d1(undriven_10), .d2(undriven_10),
    .d3(undriven_10), .d4(undriven_10), .d5(undriven_18), .d6(undriven_10));  // open: shift, clk, out, clr, q0, q1, q2, q3, q4, q5, q6, d7, q7
  Shift_Register shift_register_3 (
    .shift(undriven_4), .load(undriven_11), .d0(undriven_11), .d1(undriven_11), .d2(undriven_11),
    .d3(undriven_11), .d4(undriven_11), .d5(undriven_19), .d6(undriven_11));  // open: in, clk, out, clr, q0, q1, q2, q3, q4, q5, q6, d7, q7
  Shift_Register shift_register_4 (
    .shift(undriven_5), .load(undriven_12), .d0(undriven_12), .d1(undriven_12), .d2(undriven_12),
    .d3(undriven_12), .d4(undriven_12), .d5(undriven_20), .d6(undriven_12));  // open: in, clk, out, clr, q0, q1, q2, q3, q4, q5, q6, d7, q7
  Shift_Register shift_register_5 (
    .shift(undriven_6), .load(undriven_13), .d0(undriven_13), .d1(undriven_13), .d2(undriven_13),
    .d3(undriven_13), .d4(undriven_13), .d5(undriven_21), .d6(undriven_13));  // open: in, clk, out, clr, q0, q1, q2, q3, q4, q5, q6, d7, q7
  Shift_Register shift_register_6 (
    .shift(undriven_7), .load(undriven_14), .d0(undriven_14), .d1(undriven_14), .d2(undriven_14),
    .d3(undriven_14), .d4(undriven_14), .d5(undriven_22), .d6(undriven_14));  // open: in, clk, out, clr, q0, q1, q2, q3, q4, q5, q6, d7, q7
  Shift_Register shift_register_7 (
    .shift(undriven_8), .load(undriven_15), .d0(undriven_15), .d1(undriven_15), .d2(undriven_15),
    .d3(undriven_15), .d4(undriven_15), .d5(undriven_23), .d6(undriven_15));  // open: in, clk, out, clr, q0, q1, q2, q3, q4, q5, q6, d7, q7
  Shift_Register shift_register_8 (
    .shift(undriven), .load(undriven_16), .d0(undriven_16), .d1(undriven_16), .d2(undriven_16),
    .d3(undriven_16), .d4(undriven_16), .d5(undriven_24), .d6(undriven_16));  // open: in, clk, out, clr, q0, q1, q2, q3, q4, q5, q6, d7, q7
  or or_1 (or_1_out, undriven_17, undriven_25);
  or or_2 (or_2_out, undriven_18, undriven_26);
  or or_3 (or_3_out, undriven_19, undriven_27);
  or or_4 (or_4_out, undriven_28, undriven_20);
  or or_5 (or_5_out, undriven_21, undriven_29);
  or or_6 (or_6_out, undriven_22, undriven_30);
  or or_7 (or_7_out, undriven_23, undriven_31);
  or or_8 (or_8_out, undriven_32, undriven_24);

  // Notes on the sheet:
  //   Data Input
  //   Data Input
  //   Data Input
  //   Data Input
  //   Data Input
  //   Data Input
  //   Data Input
  //   Data Input
  //   Display
  //   Display
  //   Display
  //   Display
  //   Display
  //   Display
  //   Display
  //   Display
  //   Bird Bit
  //   Bird Bit
  //   Bird Bit
  //   Bird Bit
  //   Bird Bit
  //   Bird Bit
  //   Bird Bit
  //   Bird Bit
  //   Display
  //   Display
  //   Display
  //   Display
  //   Display
  //   Display
  //   Display
  //   Display
endmodule
