// Logisim project PRNG.circ as structural Verilog: 1 circuit, main circuit main
module main (
);

  wire clock_1_out, clock_2_out, controlled_buffer_1_out, controlled_buffer_2_out, controlled_buffer_3_out,
       controlled_buffer_4_out, controlled_buffer_5_out, controlled_buffer_6_out, controlled_buffer_7_out,
       controlled_buffer_8_out, decoder_1_out0, decoder_1_out1, decoder_1_out2, decoder_1_out3,
       decoder_1_out4, decoder_1_out5, decoder_1_out6, decoder_1_out7, j_k_ff_1_q, j_k_ff_1_qn, not_1_out,
       not_2_out, not_3_out, not_4_out, not_5_out, not_6_out, not_7_out, not_8_out, not_9_out, or_1_out,
       or_2_out, or_3_out, or_4_out, or_5_out, or_6_out, or_7_out, or_8_out, ram_1_p2, ram_2_p1,
       shift_register_1_q0, shift_register_1_q2;
  wire [2:0] shift_register_1_q1;
  wire [3:0] counter_1_q;

  Clock clock_1 (.out(clock_1_out));
  Clock clock_2 (.out(clock_2_out));
  or or_1 (or_1_out, ram_1_p2, ram_2_p1);
  or or_2 (or_2_out, ram_1_p2, ram_2_p1);
  or or_3 (or_3_out, ram_1_p2, ram_2_p1);
  or or_4 (or_4_out, ram_2_p1, ram_1_p2);
  Shift_Register #(.length(4)) shift_register_1 (
    .clr(clock_2_out), .d0(counter_1_q[0]), .q0(shift_register_1_q0), .d1(counter_1_q[0]),
    .q1(shift_register_1_q1[0]), .d2(counter_1_q[0]), .q2(shift_register_1_q2), .d3(counter_1_q[0]));  // open: shift, in, clk, out, load, q3
  Counter #(.width(4), .max('hf)) counter_1 (.Q(counter_1_q), .clk(clock_1_out));  // open: load, D, count, carry, clr
  not not_1 (not_1_out, clock_2_out);
  J_K_Flip_Flop j_k_ff_1 (
    .J(1'b1), .clk(not_1_out), .K(1'b1), .Q(j_k_ff_1_q), .Qn(j_k_ff_1_qn));  // open: preset, en, reset
  or or_5 (or_5_out, ram_1_p2, ram_2_p1);
  or or_6 (or_6_out, ram_1_p2, ram_2_p1);
  or or_7 (or_7_out, ram_1_p2, ram_2_p1);
  or or_8 (or_8_out, ram_1_p2, ram_2_p1);
  not not_2 (not_2_out, decoder_1_out0);
  Decoder #(.select(3)) decoder_1 (
    .out0(decoder_1_out0), .out1(decoder_1_out1), .out2(decoder_1_out2), .out3(decoder_1_out3),
    .out4(decoder_1_out4), .out5(decoder_1_out5), .out6(decoder_1_out6), .out7(decoder_1_out7),
    .sel(shift_register_1_q1), .en(shift_register_1_q2));
  assign controlled_buffer_1_out = not_1_out ? not_2_out : 1'bz;  // Controlled_Buffer controlled_buffer_1
  not not_3 (not_3_out, decoder_1_out1);
  assign controlled_buffer_2_out = not_1_out ? not_3_out : 1'bz;  // Controlled_Buffer controlled_buffer_2
  assign controlled_buffer_3_out = not_1_out ? not_4_out : 1'bz;  // Controlled_Buffer controlled_buffer_3
  not not_4 (not_4_out, decoder_1_out2);
  not not_5 (not_5_out, decoder_1_out3);
  assign controlled_buffer_4_out = not_1_out ? not_5_out : 1'bz;  // Controlled_Buffer controlled_buffer_4
  not not_6 (not_6_out, decoder_1_out4);
  assign controlled_buffer_5_out = not_1_out ? not_6_out : 1'bz;  // Controlled_Buffer controlled_buffer_5
  not not_7 (not_7_out, decoder_1_out5);
  assign controlled_buffer_6_out = not_1_out ? not_7_out : 1'bz;  // Controlled_Buffer controlled_buffer_6
  assign controlled_buffer_7_out = not_1_out ? not_8_out : 1'bz;  // Controlled_Buffer controlled_buffer_7
  not not_8 (not_8_out, decoder_1_out6);
  not not_9 (not_9_out, decoder_1_out7);
  assign controlled_buffer_8_out = not_1_out ? not_9_out : 1'bz;  // Controlled_Buffer controlled_buffer_8
  // RAM #(.addrWidth(2)) ram_1: pin names not known; wires that end beside it: controlled_buffer_8_out, ram_1_p2, j_k_ff_1_q, controlled_buffer_5_out, controlled_buffer_6_out, controlled_buffer_7_out, controlled_buffer_4_out, controlled_buffer_3_out, controlled_buffer_2_out, controlled_buffer_1_out
  // RAM #(.addrWidth(2)) ram_2: pin names not known; wires that end beside it: ram_2_p1, j_k_ff_1_qn, controlled_buffer_5_out, controlled_buffer_4_out, controlled_buffer_3_out, controlled_buffer_2_out, controlled_buffer_1_out
  // Pins of 1 and 3 bits meet at shift_register_1_q1
  // Pins of 1 and 4 bits meet at counter_1_q

  // Notes on the sheet:
  //   8
  //   8
  //   Clock for shifting
  //   Shift Register Row 1
  //   Shift Register Row 2
  //   Shift Register Row 3
  //   Shift Register Row 4
  //   Shift Register Row 5
  //   Shift Register Row 6
  //   Shift Register Row 7
  //   Shift Register Row 8
endmodule
